// Logisim project adder_mux.circ as structural Verilog: 1 circuit, main circuit main
module main (
  input  [3:0] in_1,
  input  [3:0] in_2,
  input  [7:0] \数据入 ,
  output out_4,
  output [7:0] out_5
);

  wire adder_1_cout, and_1_out, and_2_out, and_3_out, and_4_out, and_5_out, and_6_out, and_7_out, and_8_out,
       and_9_out, clock_1_out, d_ff_1_qn, d_ff_2_qn, multiplexer_1_out, multiplexer_2_out, not_1_out,
       or_1_out, or_2_out;
  wire [1:0] d_ff_2_q;
  wire [7:0] adder_1_out, controlled_buffer_1_out, register_2_q;

  Register #(.width(1), .trigger("falling")) register_1 (
    .D(adder_1_cout), .Q(out_4), .clk(and_1_out), .clr(and_8_out));  // open: en
  and and_1 (and_1_out, and_9_out, not_1_out);
  and and_2 (and_2_out, or_1_out, not_1_out);
  Register #(.trigger("falling")) register_2 (.D(\数据入 ), .Q(register_2_q), .clk(and_2_out));  // open: en, clr
  Adder adder_1 (.a(register_2_q), .b(controlled_buffer_1_out), .out(adder_1_out), .cout(adder_1_cout));  // open: cin
  assign controlled_buffer_1_out = or_2_out ? out_5 : 8'bz;  // Controlled_Buffer controlled_buffer_1
  and and_3 (and_3_out, not_1_out, or_2_out);
  Register #(.trigger("falling")) register_3 (
    .D(adder_1_out), .Q(out_5), .clk(and_3_out), .clr(and_8_out));  // open: en
  not not_1 (not_1_out, clock_1_out);
  Clock clock_1 (.out(clock_1_out));
  and and_4 (and_4_out, d_ff_1_qn, d_ff_2_qn);
  or or_1 (or_1_out, and_4_out, and_5_out);
  and and_5 (and_5_out, d_ff_2_q[1], d_ff_2_qn);
  D_Flip_Flop d_ff_1 (
    .clk(clock_1_out), .D(multiplexer_2_out), .Q(d_ff_2_q[1]), .Qn(d_ff_1_qn));  // open: preset, en, reset
  or or_2 (or_2_out, and_6_out, and_7_out);
  and and_6 (and_6_out, d_ff_1_qn, d_ff_2_q[0]);
  and and_7 (and_7_out, d_ff_2_q[1], d_ff_2_q[0]);
  D_Flip_Flop d_ff_2 (
    .clk(clock_1_out), .D(multiplexer_1_out), .Q(d_ff_2_q[0]), .Qn(d_ff_2_qn));  // open: preset, en, reset
  and and_8 (and_8_out, d_ff_2_qn, d_ff_1_qn);
  and and_9 (and_9_out, d_ff_2_q[1], d_ff_2_q[0]);
  Multiplexer #(.select(2)) multiplexer_1 (
    .in0(in_1[0]), .in1(in_1[1]), .in2(in_1[2]), .in3(in_1[3]), .out(multiplexer_1_out), .sel(d_ff_2_q));  // open: en
  Multiplexer #(.select(2)) multiplexer_2 (
    .in0(in_2[0]), .in1(in_2[1]), .in2(in_2[2]), .in3(in_2[3]), .out(multiplexer_2_out), .sel(d_ff_2_q));  // open: en

  // Notes on the sheet:
  //   CLR
  //   LDC
  //   T2
  //   LDA
  //   C
  //   A
  //   LDB
  //   mux型加法器
  //   B
  //   mux型加法器
  //   CLK
  //   B
  //   LDA
  //   B!
  //   LDB&ADD
  //   A
  //   mux型控制器
  //   CLR
  //   A!
  //   LDC
endmodule
