// Logisim project adder.circ as structural Verilog: 1 circuit, main circuit main
module main (
  input  [7:0] \数据入 ,
  output out_2,
  output [7:0] out_3
);

  wire adder_1_cout, and_1_out, and_2_out, and_3_out, clock_1_out, d_ff_1_q, d_ff_2_q, d_ff_3_q, d_ff_4_q,
       nor_1_out, not_1_out, or_1_out, or_2_out, or_3_out;
  wire [7:0] adder_1_out, controlled_buffer_1_out, register_2_q;

  Register #(.width(1), .trigger("falling")) register_1 (
    .D(adder_1_cout), .Q(out_2), .clk(and_1_out), .clr(d_ff_1_q));  // open: en
  and and_1 (and_1_out, d_ff_4_q, not_1_out);
  and and_2 (and_2_out, or_1_out, not_1_out);
  Register #(.trigger("falling")) register_2 (.D(\数据入 ), .Q(register_2_q), .clk(and_2_out));  // open: en, clr
  Adder adder_1 (.a(register_2_q), .b(controlled_buffer_1_out), .out(adder_1_out), .cout(adder_1_cout));  // open: cin
  assign controlled_buffer_1_out = or_2_out ? out_3 : 8'bz;  // Controlled_Buffer controlled_buffer_1
  and and_3 (and_3_out, not_1_out, or_2_out);
  Register #(.trigger("falling")) register_3 (.D(adder_1_out), .Q(out_3), .clk(and_3_out), .clr(d_ff_1_q));  // open: en
  not not_1 (not_1_out, clock_1_out);
  Clock clock_1 (.out(clock_1_out));
  nor nor_1 (nor_1_out, d_ff_1_q, d_ff_2_q, d_ff_3_q, d_ff_4_q);
  D_Flip_Flop d_ff_1 (.clk(clock_1_out), .D(nor_1_out), .Q(d_ff_1_q));  // open: Qn, preset, en, reset
  or or_1 (or_1_out, d_ff_1_q, d_ff_3_q);
  or or_2 (or_2_out, d_ff_2_q, d_ff_4_q);
  D_Flip_Flop d_ff_2 (.clk(clock_1_out), .D(d_ff_1_q), .Q(d_ff_2_q));  // open: Qn, preset, en, reset
  D_Flip_Flop d_ff_3 (.clk(clock_1_out), .D(or_3_out), .Q(d_ff_3_q));  // open: Qn, preset, en, reset
  or or_3 (or_3_out, d_ff_2_q, d_ff_4_q);
  D_Flip_Flop d_ff_4 (.clk(clock_1_out), .D(d_ff_3_q), .Q(d_ff_4_q));  // open: Qn, preset, en, reset

  // Notes on the sheet:
  //   CLR
  //   LDC
  //   T2
  //   LDA
  //   C
  //   A
  //   加法累加器
  //   LDB
  //   B
  //   加法累加器及其定序型控制器
  //   CLK
  //   LDA
  //   LDB&ADD
  //   定序型控制器
  //   CLR
  //   LDC
endmodule
