// Logisim project adder.circ as structural Verilog: 1 circuit, main circuit main
module main (
  input  [7:0] \数据入 ,
  output out_2,
  output [7:0] out_3
);

  wire adder_1_cout, and_1_out, and_2_out, and_3_out, and_4_out, and_5_out, and_6_out, clock_1_out, d_ff_1_q,
       d_ff_1_qn, d_ff_2_q, d_ff_2_qn, nor_1_out, not_1_out, or_1_out, or_2_out, or_3_out, xor_1_out;
  wire [7:0] adder_1_out, controlled_buffer_1_out, register_2_q;

  Register #(.width(1), .trigger("falling")) register_1 (
    .D(adder_1_cout), .Q(out_2), .clk(and_1_out), .clr(nor_1_out));  // open: en
  and and_1 (and_1_out, and_6_out, not_1_out);
  and and_2 (and_2_out, or_1_out, not_1_out);
  Register #(.trigger("falling")) register_2 (.D(\数据入 ), .Q(register_2_q), .clk(and_2_out));  // open: en, clr
  Adder adder_1 (.a(register_2_q), .b(controlled_buffer_1_out), .out(adder_1_out), .cout(adder_1_cout));  // open: cin
  assign controlled_buffer_1_out = xor_1_out ? out_3 : 8'bz;  // Controlled_Buffer controlled_buffer_1
  and and_3 (and_3_out, not_1_out, xor_1_out);
  Register #(.trigger("falling")) register_3 (
    .D(adder_1_out), .Q(out_3), .clk(and_3_out), .clr(nor_1_out));  // open: en
  not not_1 (not_1_out, clock_1_out);
  Clock clock_1 (.out(clock_1_out));
  and and_4 (and_4_out, d_ff_1_qn, d_ff_2_qn);
  or or_1 (or_1_out, and_4_out, and_5_out);
  and and_5 (and_5_out, d_ff_1_q, d_ff_2_q);
  D_Flip_Flop d_ff_1 (.clk(clock_1_out), .D(or_3_out), .Q(d_ff_1_q), .Qn(d_ff_1_qn));  // open: preset, en, reset
  xor xor_1 (xor_1_out, d_ff_1_q, d_ff_2_q);
  D_Flip_Flop d_ff_2 (.clk(clock_1_out), .D(or_2_out), .Q(d_ff_2_q), .Qn(d_ff_2_qn));  // open: preset, en, reset
  nor nor_1 (nor_1_out, d_ff_2_q, d_ff_1_q);
  or or_2 (or_2_out, d_ff_2_q, d_ff_1_q);
  or or_3 (or_3_out, d_ff_1_qn, d_ff_2_qn);
  and and_6 (and_6_out, d_ff_1_q, d_ff_2_qn);

  // Notes on the sheet:
  //   CLR
  //   LDC
  //   T2
  //   LDA
  //   C
  //   A
  //   LDB
  //   B
  //   CLK
  //   B
  //   LDA
  //   B!
  //   LDB&ADD
  //   A
  //   CLR
  //   A!
  //   LDC
endmodule
