// Logisim project camparer.circ as structural Verilog: 1 circuit, main circuit main
module main (
  input  in_1,
  input  in_2,
  input  A__B,
  input  [3:0] in_4,
  input  in_5,
  input  in_6,
  input  A_B,
  output out_8
);

  wire and_1_out, and_2_out, and_3_out, and_4_out, and_5_out, and_6_out, clock_1_out, clock_2_out, d_ff_1_qn,
       d_ff_2_qn, multiplexer_1_out, multiplexer_2_out, not_1_out, not_2_out, or_1_out;
  wire [1:0] d_ff_1_q;
  wire [3:0] controlled_buffer_1_out, controlled_buffer_2_out, register_1_q, register_2_q;

  not not_1 (not_1_out, out_8);
  or or_1 (or_1_out, and_1_out, and_3_out);
  and and_1 (and_1_out, d_ff_1_qn, d_ff_2_qn);
  Multiplexer #(.select(2)) multiplexer_1 (
    .in0(in_1), .in1(in_2), .in2(A__B), .in3(not_1_out), .out(multiplexer_1_out), .sel(d_ff_1_q));  // open: en
  Multiplexer #(.select(2)) multiplexer_2 (
    .in0(in_5), .in1(in_6), .in2(A_B), .in3(out_8), .out(multiplexer_2_out), .sel(d_ff_1_q));  // open: en
  and and_2 (and_2_out, or_1_out, not_2_out);
  and and_3 (and_3_out, d_ff_1_qn, d_ff_1_q[1]);
  and and_4 (and_4_out, d_ff_1_q[0], d_ff_2_qn);
  D_Flip_Flop d_ff_1 (
    .clk(clock_1_out), .D(multiplexer_1_out), .Q(d_ff_1_q[0]), .Qn(d_ff_1_qn));  // open: preset, en, reset
  D_Flip_Flop d_ff_2 (
    .clk(clock_1_out), .D(multiplexer_2_out), .Q(d_ff_1_q[1]), .Qn(d_ff_2_qn));  // open: preset, en, reset
  and and_5 (and_5_out, not_2_out, and_4_out);
  and and_6 (and_6_out, d_ff_1_q[0], d_ff_1_q[1]);
  Clock clock_1 (.out(clock_1_out));
  not not_2 (not_2_out, clock_1_out);
  Clock clock_2 (.out(clock_2_out));
  assign controlled_buffer_1_out = and_6_out ? register_1_q : 4'bz;  // Controlled_Buffer controlled_buffer_1
  Register #(.width(4)) register_1 (
    .D(register_2_q), .Q(register_1_q), .clk(and_5_out), .clr(clock_2_out));  // open: en
  Register #(.width(4)) register_2 (.D(in_4), .Q(register_2_q), .clk(and_2_out), .clr(clock_2_out));  // open: en
  assign controlled_buffer_2_out = and_6_out ? register_2_q : 4'bz;  // Controlled_Buffer controlled_buffer_2
  Comparator #(.width(4)) comparator_1 (
    .a(controlled_buffer_1_out), .b(controlled_buffer_2_out), .gt(out_8));  // open: eq, lt

  // Notes on the sheet:
  //   A
  //   B
  //   LDRb
  //   T2
  //   mux型控制器
  //   LDRa
  //   CAP
  //   mux型控制器(比较器)
  //   T1
  //   CLR
  //   CAP
  //   A
  //   LDRa
  //   比较器
  //   B
  //   LDRb
  //   A>B
endmodule
