// Logisim project camparer.circ as structural Verilog: 1 circuit, main circuit main
module main (
  input  CLR,
  input  [3:0] in_2,
  output out_3
);

  wire and_1_out, and_2_out, and_3_out, and_4_out, clock_1_out, d_ff_1_q, d_ff_1_qn, d_ff_2_q, d_ff_3_q,
       d_ff_3_qn, d_ff_4_q, nand_1_out, nor_1_out, not_1_out, or_1_out, or_2_out;
  wire [3:0] controlled_buffer_1_out, controlled_buffer_2_out, register_1_q, register_2_q;

  nor nor_1 (nor_1_out, d_ff_1_q, d_ff_2_q, d_ff_3_q, d_ff_4_q);
  D_Flip_Flop d_ff_1 (.clk(clock_1_out), .D(nor_1_out), .Q(d_ff_1_q), .Qn(d_ff_1_qn), .reset(CLR));  // open: preset, en
  nand nand_1 (nand_1_out, d_ff_1_qn, d_ff_3_qn);
  and and_1 (and_1_out, d_ff_4_q, out_3);
  or or_1 (or_1_out, and_1_out, d_ff_1_q);
  and and_2 (and_2_out, nand_1_out, not_1_out);
  and and_3 (and_3_out, d_ff_4_q, out_3);
  D_Flip_Flop d_ff_2 (.clk(clock_1_out), .D(or_1_out), .Q(d_ff_2_q), .reset(CLR));  // open: Qn, preset, en
  and and_4 (and_4_out, not_1_out, d_ff_2_q);
  or or_2 (or_2_out, and_3_out, d_ff_2_q);
  D_Flip_Flop d_ff_3 (.clk(clock_1_out), .D(or_2_out), .Q(d_ff_3_q), .Qn(d_ff_3_qn), .reset(CLR));  // open: preset, en
  D_Flip_Flop d_ff_4 (.clk(clock_1_out), .D(d_ff_3_q), .Q(d_ff_4_q), .reset(CLR));  // open: Qn, preset, en
  Clock clock_1 (.out(clock_1_out));
  not not_1 (not_1_out, clock_1_out);
  assign controlled_buffer_1_out = d_ff_4_q ? register_1_q : 4'bz;  // Controlled_Buffer controlled_buffer_1
  Register #(.width(4)) register_1 (.D(register_2_q), .Q(register_1_q), .clk(and_4_out), .clr(CLR));  // open: en
  Register #(.width(4)) register_2 (.D(in_2), .Q(register_2_q), .clk(and_2_out), .clr(CLR));  // open: en
  assign controlled_buffer_2_out = d_ff_4_q ? register_2_q : 4'bz;  // Controlled_Buffer controlled_buffer_2
  Comparator #(.width(4)) comparator_1 (
    .a(controlled_buffer_1_out), .b(controlled_buffer_2_out), .gt(out_3));  // open: eq, lt

  // Notes on the sheet:
  //   !(A>B)
  //   a
  //   LDRb
  //   A>B
  //   T2
  //   b
  //   定序型控制器
  //   LDRa
  //   c
  //   定序型控制器(比较器)
  //   CAP
  //   d
  //   T1
  //   CAP
  //   A
  //   LDRa
  //   比较器
  //   B
  //   LDRb
  //   A>B
endmodule
