// Logisim project camparer.circ as structural Verilog: 1 circuit, main circuit main
module main (
  input  [3:0] in_1,
  output out_2
);

  wire and_1_out, and_2_out, and_3_out, and_4_out, and_5_out, and_6_out, and_7_out, and_8_out, clock_1_out,
       clock_2_out, d_ff_1_q, d_ff_1_qn, d_ff_2_q, d_ff_2_qn, not_1_out, not_2_out, or_1_out, or_2_out;
  wire [3:0] controlled_buffer_1_out, controlled_buffer_2_out, register_1_q, register_2_q;

  and and_1 (and_1_out, d_ff_1_q, not_1_out, d_ff_2_q);
  not not_1 (not_1_out, out_2);
  and and_2 (and_2_out, d_ff_1_q, d_ff_2_qn);
  or or_1 (or_1_out, and_1_out, d_ff_1_qn);
  and and_3 (and_3_out, and_2_out, not_2_out);
  or or_2 (or_2_out, and_4_out, and_5_out, and_6_out);
  and and_4 (and_4_out, d_ff_1_q, d_ff_2_qn);
  and and_5 (and_5_out, d_ff_1_q, out_2, d_ff_2_q);
  D_Flip_Flop d_ff_1 (
    .clk(clock_1_out), .D(or_1_out), .Q(d_ff_1_q), .Qn(d_ff_1_qn), .reset(clock_2_out));  // open: preset, en
  and and_6 (and_6_out, d_ff_1_qn, d_ff_2_q);
  D_Flip_Flop d_ff_2 (
    .clk(clock_1_out), .D(or_2_out), .Q(d_ff_2_q), .Qn(d_ff_2_qn), .reset(clock_2_out));  // open: preset, en
  and and_7 (and_7_out, not_2_out, d_ff_1_qn);
  and and_8 (and_8_out, d_ff_2_q, d_ff_1_q);
  Clock clock_1 (.out(clock_1_out));
  not not_2 (not_2_out, clock_1_out);
  Clock clock_2 (.out(clock_2_out));
  assign controlled_buffer_1_out = and_8_out ? register_1_q : 4'bz;  // Controlled_Buffer controlled_buffer_1
  Register #(.width(4)) register_1 (
    .D(register_2_q), .Q(register_1_q), .clk(and_3_out), .clr(clock_2_out));  // open: en
  Register #(.width(4)) register_2 (.D(in_1), .Q(register_2_q), .clk(and_7_out), .clr(clock_2_out));  // open: en
  assign controlled_buffer_2_out = and_8_out ? register_2_q : 4'bz;  // Controlled_Buffer controlled_buffer_2
  Comparator #(.width(4)) comparator_1 (
    .a(controlled_buffer_1_out), .b(controlled_buffer_2_out), .gt(out_2));  // open: eq, lt

  // Notes on the sheet:
  //   A
  //   LDRA
  //   B
  //   计数型控制器
  //   LDRB
  //   CAP
  //   计数型控制器(比较器)
  //   T1
  //   CLR
  //   CAP
  //   A
  //   LDRa
  //   比较器
  //   B
  //   LDRb
  //   A>B
endmodule
