// Logisim project 逻辑控制图.circ as structural Verilog: 1 circuit, main circuit main
module main (
  input  CLR,
  input  Rst,
  input  mode,
  input  Ena,
  output INIT,
  output LDV,
  output TDISP,
  output LDM
);

  wire and_1_out, and_2_out, and_3_out, and_4_out, and_5_out, and_6_out, and_7_out, and_8_out, and_9_out,
       clock_1_out, d_ff_1_q, d_ff_1_qn, d_ff_2_q, d_ff_2_qn, not_1_out, or_1_out, or_2_out, or_3_out,
       or_4_out;

  or or_1 (or_1_out, and_1_out, and_2_out);
  D_Flip_Flop d_ff_1 (.clk(clock_1_out), .D(or_1_out), .Q(d_ff_1_q), .Qn(d_ff_1_qn), .reset(CLR));  // open: preset, en
  and and_1 (and_1_out, d_ff_1_qn, d_ff_2_qn, Ena);
  and and_2 (and_2_out, d_ff_2_q, d_ff_1_qn, Rst);
  and and_3 (and_3_out, d_ff_2_q, d_ff_1_qn, Rst);
  or or_2 (or_2_out, and_3_out, and_4_out);
  and and_4 (and_4_out, mode, d_ff_1_q, d_ff_2_qn);
  D_Flip_Flop d_ff_2 (.clk(clock_1_out), .D(or_2_out), .Q(d_ff_2_q), .Qn(d_ff_2_qn), .reset(CLR));  // open: preset, en
  Clock clock_1 (.out(clock_1_out));
  not not_1 (not_1_out, clock_1_out);
  and and_5 (and_5_out, d_ff_1_q, d_ff_2_qn);
  and and_6 (and_6_out, d_ff_2_q, d_ff_1_qn);
  and and_7 (and_7_out, d_ff_1_q, d_ff_2_q);
  or or_3 (or_3_out, and_5_out, and_6_out, and_7_out);
  and and_8 (and_8_out, d_ff_2_q, d_ff_1_qn);
  and and_9 (and_9_out, d_ff_1_q, d_ff_2_q);
  and and_10 (INIT, d_ff_2_qn, d_ff_1_qn, not_1_out);
  and and_11 (LDV, or_3_out, not_1_out);
  or or_4 (or_4_out, and_8_out, and_9_out);
  and and_12 (TDISP, or_4_out, not_1_out);
  and and_13 (LDM, d_ff_1_q, d_ff_2_q, not_1_out);

  // Notes on the sheet:
  //   Rst
  //   mode
  //   A
  //   Ena
  //   Rst
  //   计数型控制器
  //   B
  //   A
  //   B
  //   !B
  //   !A
  //   CLK
  //   子系统各个实现模块
endmodule
